// Logisim project lab1.circ as structural Verilog: 1 circuit, main circuit main
module main (
  input  x,
  input  y,
  input  z,
  output out_4
);

  wire and_1_out, and_2_out, and_3_out, and_4_out, not_1_out, not_2_out, not_3_out, not_4_out, or_1_out,
       or_2_out;

  or or_1 (or_1_out, x, y);
  not not_1 (not_1_out, x);
  not not_2 (not_2_out, z);
  not not_3 (not_3_out, or_1_out);
  and and_1 (and_1_out, not_1_out, not_2_out);
  and and_2 (and_2_out, x, z);
  not not_4 (not_4_out, y);
  and and_3 (and_3_out, not_3_out, z);
  or or_2 (or_2_out, and_1_out, and_2_out);
  and and_4 (and_4_out, or_2_out, not_4_out);
  or or_3 (out_4, and_3_out, and_4_out);
endmodule
