// Logisim project circ2.circ as structural Verilog: 1 circuit, main circuit main
module main (
  input  x3,
  input  x2,
  input  x1,
  input  x0,
  output out_5
);

  wire and_1_out, and_2_out, and_3_out, and_4_out, not_1_out, not_2_out, not_3_out, not_4_out, not_5_out;

  not not_1 (not_1_out, x3);
  not not_2 (not_2_out, x1);
  not not_3 (not_3_out, x0);
  not not_4 (not_4_out, x3);
  and and_1 (and_1_out, not_1_out, not_2_out, not_3_out);
  and and_2 (and_2_out, not_4_out, x2, x0);
  not not_5 (not_5_out, x0);
  and and_3 (and_3_out, not_1_out, x1, not_5_out);
  and and_4 (and_4_out, x0, x2, x3);
  or or_1 (out_5, and_1_out, and_2_out, and_3_out, and_4_out);
endmodule
