// Logisim project circ1.circ as structural Verilog: 1 circuit, main circuit main
module main (
  output out_1,
  output out_2,
  output out_3
);

  Comparator comparator_1 (.a(8'h5), .b(8'h2), .gt(out_1));  // open: eq, lt
  Comparator comparator_2 (.a(8'h5), .b(8'h2), .eq(out_2));  // open: gt, lt
  Comparator comparator_3 (.a(8'h5), .b(8'h2), .lt(out_3));  // open: gt, eq
endmodule
