// Logisim project circ2.circ as structural Verilog: 1 circuit, main circuit main
module main (
  input  in_1,
  input  in_2,
  input  in_3,
  input  in_4,
  input  in_5,
  input  in_6,
  input  in_7,
  input  in_8,
  input  in_9,
  input  [1:0] in_10,
  input  in_11,
  output out_12,
  output out_13
);

  wire and_1_out, and_2_out, and_3_out, and_4_out, not_1_out, not_2_out;

  not not_1 (not_1_out, in_1);
  not not_2 (not_2_out, in_2);
  Multiplexer #(.select(2)) multiplexer_1 (
    .in0(in_7), .in1(in_8), .in2(in_9), .in3(in_11), .out(out_13), .sel(in_10));  // open: en
  and and_1 (and_1_out, in_3, not_1_out, not_2_out);
  and and_2 (and_2_out, in_4, not_1_out, in_2);
  and and_3 (and_3_out, in_5, in_1, not_2_out);
  and and_4 (and_4_out, in_6, in_1, in_2);
  or or_1 (out_12, and_1_out, and_2_out, and_3_out, and_4_out);
endmodule
