// Logisim project circ3.circ as structural Verilog: 1 circuit, main circuit main
module main (
  input  in_1,
  input  in_2,
  input  in_3,
  input  in_4,
  input  [1:0] in_5,
  output out_6,
  output out_7,
  output out_8,
  output out_9
);

  wire demultiplexer_1_out0, demultiplexer_1_out1, demultiplexer_1_out2, demultiplexer_1_out3, not_1_out,
       not_2_out;

  not not_1 (not_1_out, in_1);
  not not_2 (not_2_out, in_2);
  Demultiplexer #(.select(2)) demultiplexer_1 (
    .out0(demultiplexer_1_out0), .out1(demultiplexer_1_out1), .out2(demultiplexer_1_out2),
    .out3(demultiplexer_1_out3), .in(in_4), .sel(in_5));  // open: en
  and and_1 (out_6, in_3, not_1_out, not_2_out);
  and and_2 (out_7, in_3, not_1_out, in_2);
  and and_3 (out_8, in_3, in_1, not_2_out);
  and and_4 (out_9, in_3, in_1, in_2);
endmodule
