// Logisim project circ2.circ as structural Verilog: 1 circuit, main circuit main
module main (
  input  in_1,
  input  in_2,
  input  [2:0] in_3,
  output out_4
);

  wire not_1_out;

  not not_1 (not_1_out, in_2);
  Multiplexer #(.select(3)) multiplexer_1 (
    .in0(in_1), .in1(in_2), .in2(in_1), .in3(in_2), .in4(in_1), .in5(not_1_out), .in6(in_1), .in7(in_1),
    .out(out_4), .sel(in_3));  // open: en
endmodule
