// Logisim project circ4.circ as structural Verilog: 1 circuit, main circuit main
module main (
  input  in_1,
  input  in_2,
  input  [2:0] in_3,
  output out_4
);

  wire not_1_out, not_2_out;

  not not_1 (not_1_out, in_2);
  not not_2 (not_2_out, in_1);
  Multiplexer #(.select(3)) multiplexer_1 (
    .in0(in_2), .in1(not_1_out), .in2(not_2_out), .in3(not_1_out), .in4(in_2), .in5(in_2), .in6(in_2),
    .in7(in_1), .out(out_4), .sel(in_3));  // open: en
endmodule
