// Logisim project circ5.circ as structural Verilog: 1 circuit, main circuit main
module main (
  input  in_1,
  input  in_2,
  input  in_3,
  input  [1:0] in_4,
  output out_5
);

  wire not_1_out, not_2_out, or_1_out, or_2_out;

  not not_1 (not_1_out, in_2);
  not not_2 (not_2_out, in_3);
  or or_1 (or_1_out, not_1_out, in_3);
  or or_2 (or_2_out, in_2, not_2_out);
  Multiplexer #(.select(2)) multiplexer_1 (
    .in0(in_1), .in1(or_1_out), .in2(or_2_out), .in3(in_2), .out(out_5), .sel(in_4));  // open: en
endmodule
