// Logisim project circ1.circ as structural Verilog: 1 circuit, main circuit main
module main (
  output [7:0] out_1,
  output out_2,
  output [7:0] out_3,
  output out_4,
  output [7:0] out_5,
  output out_6,
  output [7:0] out_7,
  output out_8,
  output [7:0] out_9,
  output out_10
);

  Adder adder_1 (.a(8'h3), .b(8'h5), .out(out_1), .cout(out_2));  // open: cin
  Adder adder_2 (.a(8'ha), .b(8'h5), .out(out_3), .cout(out_4));  // open: cin
  Adder adder_3 (.a(8'h12), .b(8'h6), .out(out_5), .cout(out_6));  // open: cin
  Adder adder_4 (.a(8'h8), .b(8'h8), .out(out_7), .cout(out_8));  // open: cin
  Adder adder_5 (.a(8'h5), .b(8'h7), .out(out_9), .cout(out_10));  // open: cin
endmodule
