// Logisim project circ2.circ as structural Verilog: 1 circuit, main circuit main
module main (
  input  in_1,
  input  in_2,
  input  in_3,
  input  in_4,
  input  in_5,
  output [7:0] out_6,
  output out_7,
  output [7:0] out_8,
  output out_9,
  output [7:0] out_10,
  output out_11,
  output [7:0] out_12,
  output out_13,
  output [7:0] out_14,
  output out_15
);

  Adder adder_1 (.a(8'h4), .b(8'h1), .out(out_6), .cin(in_1), .cout(out_7));
  Adder adder_2 (.a(8'hb), .b(8'h1), .out(out_8), .cin(in_2), .cout(out_9));
  Adder adder_3 (.a(8'h12), .b(8'h4), .out(out_10), .cin(in_3), .cout(out_11));
  Adder adder_4 (.a(8'h6), .b(8'h9), .out(out_12), .cin(in_4), .cout(out_13));
  Adder adder_5 (.a(8'h3), .b(8'h7), .out(out_14), .cin(in_5), .cout(out_15));
endmodule
