// Logisim project multiplexer.circ as structural Verilog: 1 circuit, main circuit main
module main (
  input  in_1,
  input  [1:0] in_2,
  output out_3
);

  wire not_1_out, not_2_out;

  not not_1 (not_1_out, in_1);
  not not_2 (not_2_out, in_1);
  Multiplexer #(.select(2)) multiplexer_1 (
    .in0(in_1), .in1(not_2_out), .in2(not_1_out), .in3(in_1), .out(out_3), .sel(in_2));  // open: en
endmodule
