// Logisim project multiplexer_with_carry.circ as structural Verilog: 1 circuit, main circuit main
module main (
  input  in_1,
  input  in_2,
  input  [1:0] in_3,
  output out_4
);

  wire not_1_out;

  not not_1 (not_1_out, in_1);
  Multiplexer #(.select(2)) multiplexer_1 (
    .in0(not_1_out), .in1(in_2), .in2(in_2), .in3(in_1), .out(out_4), .sel(in_3));  // open: en
endmodule
