// Logisim project circ7.circ as structural Verilog: 1 circuit, main circuit main
module main (
  input  [2:0] in_1
);

  wire and_1_out, decoder_1_out0, decoder_1_out1, decoder_1_out2, decoder_1_out3, decoder_1_out4,
       decoder_1_out5, decoder_1_out6, decoder_1_out7, not_1_out, not_2_out, not_3_out, not_4_out, or_1_out,
       or_2_out;

  Decoder #(.select(3)) decoder_1 (
    .out0(decoder_1_out0), .out1(decoder_1_out1), .out2(decoder_1_out2), .out3(decoder_1_out3),
    .out4(decoder_1_out4), .out5(decoder_1_out5), .out6(decoder_1_out6), .out7(decoder_1_out7), .sel(in_1));  // open: en
  not not_1 (not_1_out, decoder_1_out0);
  not not_2 (not_2_out, decoder_1_out3);
  not not_3 (not_3_out, decoder_1_out6);
  not not_4 (not_4_out, decoder_1_out5);
  or or_1 (or_1_out, decoder_1_out1, decoder_1_out2, decoder_1_out4, decoder_1_out7);
  or or_2 (or_2_out, not_1_out, not_2_out, not_4_out, not_3_out);
  and and_1 (and_1_out, or_1_out, or_2_out);
endmodule
