// Logisim project lab7_1.circ as structural Verilog: 1 circuit, main circuit main
module main (
  input  D0,
  input  D1,
  input  D2,
  input  D3,
  output A,
  output B
);

  or or_1 (A, D1, D3);
  or or_2 (B, D2, D3);
endmodule
