// Logisim project lab7_2.circ as structural Verilog: 1 circuit, main circuit main
module main (
  input  D1,
  input  D2,
  input  D3,
  input  D4,
  input  D5,
  input  D6,
  input  D7,
  output A,
  output B,
  output C
);

  or or_1 (A, D4, D5, D6, D7);
  or or_2 (B, D2, D3, D6, D7);
  or or_3 (C, D1, D3, D5, D7);
endmodule
