// Logisim project lab7_3.circ as structural Verilog: 1 circuit, main circuit main
module main (
  input  in_1,
  input  in_2,
  input  in_3,
  input  in_4,
  output [1:0] out_5,
  output out_6
);

  Priority_Encoder #(.select(2)) priority_encoder_1 (
    .in0(in_4), .in1(in_3), .in2(in_2), .in3(in_1), .out(out_5), .gs(out_6));  // open: en_out, en_in
endmodule
