// Logisim project circ1.circ as structural Verilog: 1 circuit, main circuit main
module main (
  input  D0,
  input  D1,
  input  D2,
  input  D3,
  output V,
  output A,
  output B
);

  wire and_1_out, not_1_out;

  not not_1 (not_1_out, D2);
  or or_1 (V, D0, D1, D2, D3);
  or or_2 (A, D2, D3);
  and and_1 (and_1_out, not_1_out, D1);
  or or_3 (B, and_1_out, D3);
endmodule
