// Logisim project lab8_1.circ as structural Verilog: 1 circuit, main circuit main
module main (
  input  D0,
  input  D1,
  input  D2,
  input  D3,
  output V,
  output A,
  output B
);

  wire and_1_out;

  and and_1 (and_1_out, D1, D2);
  or or_1 (V, D0, D1, D2, D3);
  or or_2 (A, D2, D3);
  or or_3 (B, D3, and_1_out);
endmodule
