// Logisim project j-k.circ as structural Verilog: 1 circuit, main circuit main
module main (
  input  J,
  input  in_2,
  input  K,
  input  in_4,
  input  in_5,
  output out_6,
  output out_7
);

  wire and_1_out, and_2_out, clock_1_out, j_k_ff_1_q, j_k_ff_1_qn;

  and and_1 (and_1_out, out_7, J, in_2);
  and and_2 (and_2_out, in_2, K, out_6);
  Clock clock_1 (.out(clock_1_out));
  nand nand_1 (out_6, and_1_out, out_7);
  nand nand_2 (out_7, out_6, and_2_out);
  J_K_Flip_Flop j_k_ff_1 (
    .J(in_4), .K(in_5), .Q(j_k_ff_1_q), .Qn(j_k_ff_1_qn), .en(clock_1_out));  // open: clk, preset, reset
endmodule
