// Logisim project lab9_1.circ as structural Verilog: 1 circuit, main circuit main
module main (
  input  in_1,
  output out_2,
  output out_3
);

  wire clock_1_out;

  Clock clock_1 (.out(clock_1_out));
  nor nor_1 (out_2, in_1, out_3);
  nor nor_2 (out_3, out_2, clock_1_out);
endmodule
