// Logisim project lab9_2.circ as structural Verilog: 1 circuit, main circuit main
module main (
  input  in_1,
  input  in_2,
  input  in_3,
  input  in_4,
  output out_5,
  output out_6,
  output out_7,
  output out_8
);

  wire clock_1_out, nand_1_out, nand_2_out;

  Clock clock_1 (.out(clock_1_out));
  nand nand_1 (nand_1_out, in_1, in_2);
  nand nand_2 (nand_2_out, in_2, in_3);
  J_K_Flip_Flop j_k_ff_1 (.J(in_4), .K(clock_1_out), .Q(out_7), .Qn(out_8));  // open: clk, preset, en, reset
  nand nand_3 (out_5, nand_1_out, out_6);
  nand nand_4 (out_6, out_5, nand_2_out);
endmodule
