// Logisim project r-s.circ as structural Verilog: 1 circuit, main circuit main
module main (
  input  in_1,
  input  in_2,
  input  in_3,
  input  in_4,
  input  in_5,
  input  in_6,
  output out_7,
  output out_8
);

  wire and_1_out, and_2_out, not_3_out, not_4_out, or_1_out, or_2_out, s_r_ff_1_q, s_r_ff_1_qn;

  S_R_Flip_Flop s_r_ff_1 (.S(in_2), .R(in_3), .Q(s_r_ff_1_q), .Qn(s_r_ff_1_qn));  // open: clk, preset, reset, en
  or or_1 (or_1_out, in_5, out_8);
  or or_2 (or_2_out, out_7, in_6);
  not not_1 (out_7, or_1_out);
  not not_2 (out_8, or_2_out);
  and and_1 (and_1_out, in_1, not_4_out);
  and and_2 (and_2_out, not_3_out, in_4);
  not not_3 (not_3_out, and_1_out);
  not not_4 (not_4_out, and_2_out);
endmodule
