// Logisim project laboratorul 4.circ as structural Verilog: 1 circuit, main circuit main
module main (
  input  x1,
  input  x2,
  input  x3,
  input  in_4,
  output out_5,
  output [3:0] out_6
);

  wire and_1_out, and_2_out, and_3_out, and_4_out, not_1_out, not_2_out, not_3_out, not_4_out, not_5_out,
       not_6_out, not_7_out, not_8_out;

  not not_1 (not_1_out, x1);
  not not_2 (not_2_out, x2);
  not not_3 (not_3_out, x3);
  not not_4 (not_4_out, x2);
  not not_5 (not_5_out, x1);
  not not_6 (not_6_out, x2);
  not not_7 (not_7_out, x1);
  not not_8 (not_8_out, x3);
  Multiplexer #(.width(4)) multiplexer_1 (.in0(4'b0001), .in1(4'b0001), .out(out_6), .sel(in_4));  // open: en
  and and_1 (and_1_out, not_1_out, not_2_out, not_3_out);
  and and_2 (and_2_out, x1, not_4_out, x3);
  and and_3 (and_3_out, not_5_out, not_6_out, x3);
  and and_4 (and_4_out, not_7_out, not_8_out);
  or or_1 (out_5, and_1_out, and_2_out, and_3_out, and_4_out);
endmodule
